# Fritzing sketch esquema (saved by Fritzing 0.9.5d)
breadboards: 1

parts:
  A1 = tds-sensor-meter-v1.0_1
  M1 = ph-4502c [package=THT]
  DS1 = DS18B20 1-Wire Temperature Sensor Probe
  U1 = ESP32-38PinWide [part_number=ESP32-38PinWide]
  RHT1 = Humidity and Temperature Sensor RHT03
  RHT2 = Humidity and Temperature Sensor RHT03
  R1 = Resistor [tolerance=±5% resistance=4.7k package=THT]

nets:
  N1: A1.pin1, U1.GPIO33
  VCC: A1.pin2, M1.pin6, DS1.VDD, RHT1.Vcc, RHT2.Vcc, R1.Pin_0
  N2: A1.pin3, M1.pin4, M1.pin5, DS1.GND, RHT1.GND_1, RHT2.GND_1
  N3: M1.pin3, U1.GPIO34
  N4: DS1.DQ, U1.GPIO4, R1.Pin_1
  N5: U1.GPIO12, RHT2.Data-signal
  N6: U1.GPIO13, RHT1.Data-signal

custom parts:
  : TDS Meter V1.0 Development Board Water Meter Filter Measuring Water Sensor Module.
  ph-4502c: ph-4502c PH Meter.
  ESP32-38PinWide: Generic 38-Pin ESP32 with wide format (only access to one side of pins on a breadboard) based on Stephen Lilley's HiLetgo ESP-WROOM-32 ESP32 ESP-32S Development Board.
